# Fritzing sketch arduino_tascam_serial_midi (saved by Fritzing 0.9.3b)
breadboards: 1

parts:
  Part1 = Arduino Uno (Rev3) - ICSP
  Part2 = SparkFun MIDI Shield  # not connected
  R1 = Resistor [tolerance=±5% resistance=220 package=THT]
  C1 = Electrolytic Capacitor [capacitance=1µF package="100 mil [THT, electrolytic]"]
  CD4048B1 = CD4048B [part_number=CD4048B package="DIP (Dual Inline) [THT]"]
  C2 = Ceramic Capacitor [capacitance=100nF package="100 mil [THT, multilayer]"]
  R2 = Resistor [tolerance=±5% resistance=220 package="2010 [SMD]"]
  J1 = Dagu DGServo 9g header (male) [package=THT]

nets:
  N1: Part1.ICSP_MOSI, Part1.D11_PWM/MOSI, CD4048B1.H
  GND: Part1.GND, C1.-, CD4048B1.VSS, J1.gnd
  N2: Part1.5V, C1.+, CD4048B1.J
  N3: Part1.D8, CD4048B1.E, R2.Pin_0
  N4: Part1.D10_PWM/SS, CD4048B1.G
  N5: R1.Pin_0, CD4048B1.Kb, R2.Pin_1
  N6: R1.Pin_1, C2.0
  N7: CD4048B1.Kd, J1.Vcc
  N8: CD4048B1.F, J1.pulse

notes:
  This header represents ground, receive and send from the serial port
  This is the LTC drive circuit. It converts the audio to useable levels

// code stored in the sketch: MIDI_CONFIG.ino

volatile byte lastPlayStatus = 0;//needed for record toggle

// -----------------------------------------------------------------------------
//MIDI callback section
// This function will be automatically called when a MIDI message is received.
// It must be a void-returning function with the correct parameters,
// see documentation here:
// http://arduinomidilib.fortyseveneffects.com/a00022.html

//All commands are CC for simplicity sake

void handleControlChange(byte channel, byte number, byte value)
{
  byte lastNumber;//tracks last valid CC
  byte lastValue;//tracks last valid value
  if (channel == CC_CHANNEL)
  {
    switch (number) {//reassign CCs as needed for your application

      
      //Record toggle Track indicated - possible to poll for active tracks by
      // sending @2 and parsing the right nibble - not implemented
      // tracks 1,2,3,4 are byte 2, tracks 5,6,7,8 are byte 3
      case 0x14:
        {
          SerialOne.println("C1");//record on
        }
        break;
      case 0x15:
        {
          SerialOne.println("C2");//record on
        }
        break;
      case 0x16:
        {
          SerialOne.println("C3");//record on
        }
        break;
      case 0x17:
        {
          SerialOne.println("C4");//record on
        }
        break;
      case 0x18:
        {
          SerialOne.println("C5");//record on
        }
        break;
      case 0x19:
        {
          SerialOne.println("C6");//record on
        }
        break;
      case 0x1A:
        {
          SerialOne.println("C7");//record on
        }
        break;
      case 0x1B:
        {
          SerialOne.println("C8");//record on
        }
        break;
      case 0x32: //Record Strobe
        if (value != 0x0 && lastPlayStatus == 1)
        {
          SerialOne.println('V');//Play record on
        }

        else if (value !=0x0 && lastPlayStatus != 1)
        {
          SerialOne.println('Y');//Pause record on
        }
        else if (value == 0)
        {
          SerialOne.println('W');//record off-does not work from pause
        }
        break;
      //end of recording

      //transport controls
      case 0x33://stop can also be handled by callback
        if (value == 0x0)
        {      
        SerialOne.println('S');//stop
        lastPlayStatus = 0;
        }
        break;

      case 0x36://can also be handled by callback
        if (value == 0x0)
        {
          if (lastPlayStatus != 1)
          {
            SerialOne.println('P');//play
            lastPlayStatus = 1;
          }
          else if (lastPlayStatus == 1)
          {
            SerialOne.println('X');//pause
            lastPlayStatus = 0;
          }
        }
        break;

      case 0x09://Rewind & FF
      if (value !=0)
      {
        if (value <= 0x32)
        {
          SerialOne.println('R');
        }
        else
        {
          SerialOne.println('Q');
        }
         lastPlayStatus = 0;
      }
        break;

      case 0x1c://Repeat toggle
          SerialOne.write(0x5C);     
        break;
        
      case 0x39://set memo 1
          SerialOne.println("E1");
        break;
      case 0x3A://set memo 2
          SerialOne.println("E2");
        break;
        
      case 0x3B://set Monitor Mode Insert
      if (value > 0x00)
      {
          SerialOne.println("O2");
      }
        break;      

      case 0x3C://set Mix Mode Insert
      if (value > 0x00)
      {
          SerialOne.println("O3");
      }
        break;   
                
      case 0x3D://Display Change
      if (value > 0x00)
      {
          SerialOne.println("O8");
      }
        break;  
         
      case 0x3E://Return to zero
      if (value > 0x00)
      {
          SerialOne.println("Z");
      }
        break;     
                
      case 0x7B://EMERGENCY STOP
        SerialOne.println('S');//stop
        lastPlayStatus = 0;
        break;
        
      default:
        lastNumber = number;
        lastValue = value;
    }
    lastNumber = number;
    lastValue = value;
  }
}
//void handleStart()//using CCs for now to simplify
//{
//  SerialOne.println('P');
//}
//void handleStop()
//{
//  SerialOne.println('S');
//}
//void handleContinue()
//{
//  SerialOne.println('P');
//}

void handleSystemReset()
{
  SerialOne.println('Z');
}

//Sysex MMC is a pain.  These work, but it is probably best to choose either MMC or CC
//void handleSystemExclusive(byte *array, unsigned size)
//{
//  if ((array[0] == 0xF0) && (array[size - 1] == 0xf7))
//  {
//    if (array[1] == 0x7f)
//    {
//      if ( array[2] == 0x7f)
//      {
//        switch (array[4]) {
//
//          case 0x01://F0  7F  7F  06  01  F7  stop
//
//            SerialOne.println('S');
//            break;
//
//          case 0x02://F0  7F  7F  06  02  F7 play
//            SerialOne.println('P');//play
//            break;
//
//          case 0x03://F0  7F  7F  06  03  F7 FF
//            SerialOne.println('P');//play
//            break;
//
//          case 0x06://F0  7F  7F  06  06  F7  |  MMC Record Strobe
//            SerialOne.println('V');
//            break;
//
//          case 0x07://F0  7F  7F  06  06  F7  |  MMC Record Off
//            SerialOne.println('W');
//            break;
//
//          case 0x09://F0  7F  7F  06  09  F7  |  MMC Pause
//            SerialOne.println('X');
//            break;
//
//          default:
//            SerialOne.print(array[0], HEX);
//            SerialOne.print(array[1], HEX);
//            SerialOne.print(array[2], HEX);
//            SerialOne.print(array[3], HEX);
//            SerialOne.print(array[4], HEX);
//            SerialOne.print(array[5], HEX);
//            SerialOne.println("   unknown mmc message ");
//
//        }
//      }
//    }
//  }
//}



void handleNoteOn(byte channel, byte pitch, byte velocity)
{
  // do something different depending on the range value:
  {

  }
  // Do whatever you want when a note is pressed.

  // Try to keep your callbacks short (no delays ect)
  // otherwise it would slow down the loop() and have a bad impact
  // on real-time performance.

}
void handleNoteOff(byte channel, byte pitch, byte velocity)
{
  // Do something when the note is released.
  // Note that NoteOn messages with 0 velocity are interpreted as NoteOffs.
}

// -----------------------------------------------------------------------------

//

// code stored in the sketch: SMPTE_INCLUDES.ino

//LTC stuff borrowed from Arduino forum
#define icpPin 8        // ICP input pin on arduino -not needed as handled by interrupt
#define one_time_max          475 // these values are setup for NTSC video
#define one_time_min          300 // PAL would be around 1000 for 0 and 500 for 1
#define zero_time_max         875 // 80bits times 29.97 frames per sec
#define zero_time_min         700 // equals 833 (divide by 8 clock pulses)

#define end_data_position      63
#define end_sync_position      77
#define end_smpte_position     80

volatile unsigned int bit_time;
volatile boolean valid_tc_word;
volatile boolean ones_bit_count;
volatile boolean tc_sync;
volatile boolean write_ltc_out;
volatile boolean write_mtc_out;
volatile boolean drop_frame_flag;
volatile boolean drop_frame_flag_mtc;

volatile byte total_bits;
volatile bool current_bit;
volatile byte sync_count;

volatile byte tc[8];
volatile byte timeCodeLTC[12];
char timeCodeMTC[14];
char timeCodeLTC2[14];
char df = 'n';
char dfm = 'n';
char* flag_l;
char* flag_m;
int ctr = 0;
//MTC stuff from forum
byte h_m, m_m, s_m, f_m;      //hours, minutes, seconds, frame
char h_l, m_l, s_l, f_l;      //hours, minutes, seconds, frame
byte buf_temp_mtc[8];     //timecode buffer
byte command, data, index;


/* ICR interrupt vector */
ISR(TIMER1_CAPT_vect)
{
  //toggleCaptureEdge
  TCCR1B ^= _BV(ICES1);

  bit_time = ICR1;

  //resetTimer1
  TCNT1 = 0;

  if ((bit_time < one_time_min) || (bit_time > zero_time_max)) // get rid of anything way outside the norm
  {
    total_bits = 0;
  }
  else
  {
    if (ones_bit_count == true) // only count the second ones pluse
      ones_bit_count = false;
    else
    {
      if (bit_time > zero_time_min)
      {
        current_bit = 0;
        sync_count = 0;
      }
      else if (bit_time < one_time_max)
      {
        ones_bit_count = true;
        current_bit = 1;
        sync_count++;
        if (sync_count == 12) // part of the last two bytes of a timecode word
        {
          sync_count = 0;
          tc_sync = true;
          total_bits = end_sync_position;
        }
      }

      if (total_bits <= end_data_position) // timecode runs least to most so we need
      { // to shift things around
        tc[0] = tc[0] >> 1;

        for (int n = 1; n < 8; n++)
        {
          if (tc[n] & 1)
            tc[n - 1] |= 0x80;

          tc[n] = tc[n] >> 1;
        }

        if (current_bit == 1)
          tc[7] |= 0x80;
      }
      total_bits++;
    }

    if (total_bits == end_smpte_position) // we have the 80th bit
    {
      total_bits = 0;
      if (tc_sync)
      {
        tc_sync = false;
        valid_tc_word = true;
      }
    }

    if (valid_tc_word)
    {
      valid_tc_word = false;
      timeCodeLTC[10] = (tc[0] & 0x0F) + 0x30;  // frames
      timeCodeLTC[9] = (tc[1] & 0x03) + 0x30;  // 10's of frames
      timeCodeLTC[8] =  '.';
      timeCodeLTC[7] = (tc[2] & 0x0F) + 0x30;  // seconds
      timeCodeLTC[6] = (tc[3] & 0x07) + 0x30;  // 10's of seconds
      timeCodeLTC[5] =  ':';
      timeCodeLTC[4] = (tc[4] & 0x0F) + 0x30;  // minutes
      timeCodeLTC[3] = (tc[5] & 0x07) + 0x30;  // 10's of minutes
      timeCodeLTC[2] = ':';
      timeCodeLTC[1] = (tc[6] & 0x0F) + 0x30;  // hours
      timeCodeLTC[0] = (tc[7] & 0x03) + 0x30;  // 10's of hours
      drop_frame_flag = (tc[1] & 0x04) != 0;

      if (drop_frame_flag)
      {
        df = 'd';
      }
      else
      {
        df = 'n';
      }
      sprintf(timeCodeLTC2, "LTC:%c:%s /r", df, timeCodeLTC);
      write_ltc_out = true;

    }
  }
}
void timeCodeCall()
{
  if(write_ltc_out)
  {
    if(timeCodeLTC[10]%2)//not needed for hardware serial
    {
      SerialOne.println(timeCodeLTC2);
      SerialOne.println();
    }
    write_ltc_out =false;
  }
}
void handleTimeCodeQuarterFrame(byte data)
{
  index = data >> 4;  //extract index/packet ID
  data &= 0x0F;       //clear packet ID from data
  buf_temp_mtc[index] = data;

  if (index >= 0x07) {  //recalculate timecode once FRAMES LSB quarter-frame received
    h_m = byte((buf_temp_mtc[7] & 0x01) << 4) + buf_temp_mtc[6];
    m_m = byte(buf_temp_mtc[5] << 4) + buf_temp_mtc[4];
    s_m = byte(buf_temp_mtc[3] << 4) + buf_temp_mtc[2];
    f_m = byte(buf_temp_mtc[1] << 4) + buf_temp_mtc[0];

    drop_frame_flag_mtc = (buf_temp_mtc[1] & 0x04) != 0;

    if (drop_frame_flag_mtc)
    {
      dfm = 'd';
    }
    else
    {
      dfm = 'n';
    }
    sprintf(timeCodeMTC, "MTC:%c:%.2d:%.2d:%.2d:%.2d ", dfm, h_m, m_m, s_m, f_m);
    SerialOne.println(timeCodeMTC);
    write_mtc_out = true;
  }
}

void smpteSetup()
{
  MIDI.setHandleTimeCodeQuarterFrame(handleTimeCodeQuarterFrame);
  attachInterrupt(1, TIMER1_CAPT_vect, CHANGE);
  pinMode(icpPin, INPUT);                  // ICP pin (digital pin 8 on arduino) as input
  bit_time = 0;
  valid_tc_word = false;
  ones_bit_count = false;
  tc_sync = false;
  write_ltc_out = false;
  drop_frame_flag = false;
  total_bits =  0;
  current_bit =  0;
  sync_count =  0;
  TCCR1A = B00000000; // clear all
  TCCR1B = B11000010; // ICNC1 noise reduction + ICES1 start on rising edge + CS11 divide by 8
  TCCR1C = B00000000; // clear all
  TIMSK1 = B00100000; // ICIE1 enable the icp
  TCNT1 = 0; // clear timer1
}

// code stored in the sketch: TASCAM_MIDI_SMPTE_MAIN.ino
/*   Tascam Serial Control for Midistudios and devices that use the Accessory 2 port.

   See the Readme.md for more details 
   
   The goal of this project is to create an open device that can replace the obsolete and 
   all but impossible-to-find sync devices for various Tascam tape machines.
   
   Hardware roughly required:

   Arduino compatible microcontroller
   some sort of inverter/buffer to convert the UART data to reasonable voltages for RS-232
   Opto-isolator for standard MIDI
   Obviously USB midi and Bluetooth can be used, but are not currently implemented.

   Hardware specifically used by me:
   Arduino Uno with Midi Shield
   CD 4049 inverter for converting LTC from audio to digital and two other pins for UART inversion.
   You may want to use better hardware. I had no problems.
   various resistors and caps.
   USB FTDI uart thing for debugging

  There is a pinout available in the documents, just remember to connect your transmit to the device's receive
  and to both protect and invert the inputs from the higher and lower voltages that RS-232 uses. I had great luck with 
  the 4049s and 5v, but I am not sure if 3.3v stuff would play nice.
  
   2018 Ben Gencarelle
*/
//#define TIME_SYNC 1 //comment this out for just MIDI control over serial port
//#define EXTERNAL_CONTROL 1 // to use for generalized control

#define CC_CHANNEL 1//everything on one CC makes easier
#include <MIDI.h>

#include <SoftwareSerialParity.h>// Not needed for devices with multiple UARTS
SoftwareSerialParity SerialOne(10, 11); // RX, TX
MIDI_CREATE_DEFAULT_INSTANCE();

void setup()
{
  SerialOne.begin(9600, EVEN);
  SerialOne.println('S');
  SerialOne.println();
  //Midi section//
  MIDI.setHandleNoteOn(handleNoteOn);  // Put only the name of the function
  MIDI.setHandleNoteOff(handleNoteOff);
  MIDI.setHandleControlChange(handleControlChange);
  //MIDI.setHandleStop(handleStop);
  //  MIDI.setHandleStart(handleStart);
  //  MIDI.setHandleContinue(handleContinue);
  //  MIDI.setHandleSystemExclusive(handleSystemExclusive);

  // Initiate MIDI communications, listen to all channels
  MIDI.begin(MIDI_CHANNEL_OMNI);


#if defined (TIME_SYNC)
  smpteSetup();
#endif

}

void loop()
{
  MIDI.read();
  
#if defined (TIME_SYNC)
  {
    timeCodeCall();
  }
#endif
}
